# Fritzing sketch schema_tlogger (saved by Fritzing 0.9.4)
circuit board: 8.46667cm x 5.64444cm

parts:
  WeMos_D1_Mini1 = WeMos D1 Mini
  Bauteil2 = Barometric Pressure Sensor - BMP180 Breakout (GY-68)

nets:
  3V3: WeMos_D1_Mini1.3V3, Bauteil2.VCC
  N1: WeMos_D1_Mini1.D0, WeMos_D1_Mini1.RST
  N2: WeMos_D1_Mini1.D1, Bauteil2.SCL
  N3: WeMos_D1_Mini1.D2, Bauteil2.SDA
  N4: WeMos_D1_Mini1.G, Bauteil2.GND
